// Logisim project circuit.circ as structural Verilog: 1 circuit, main circuit main
module main (
  input  man_step,
  output [7:0] out_2,
  output [7:0] out_3,
  output [15:0] out_4
);

  wire and_1_out, and_2_out, and_3_out, and_4_out, clk, clock_1_out, comparator_2_eq, comparator_2_gt,
       comparator_2_lt, comparator_5_eq, comparator_5_gt, comparator_6_lt, comparator_7_eq, comparator_7_lt,
       comparator_8_lt, comparator_9_eq, comparator_10_gt, comparator_10_lt, comparator_11_gt,
       comparator_11_lt, comparator_12_eq, comparator_12_lt, or_1_out, or_3_out, or_4_out, or_5_out,
       pull_resistor_1_node, res, reset, step_out, stop;
  wire [1:0] counter_2_q;
  wire [6:0] r1, r2, r3, subaddr;
  wire [7:0] d1, d2, d3, mainaddr, multiplexer_1_out, multiplexer_2_out, multiplexer_3_out,
       multiplexer_4_out, multiplexer_5_out, multiplier_2_out, multiplier_3_out, ram_out, subtractor_1_out,
       subtractor_2_out, subtractor_3_out, subtractor_4_out;
  wire [14:0] adder_1_out, bit_extender_1_out, bit_extender_2_out, multiplier_1_out;
  wire [15:0] bit_extender_3_out, register_7_q;

  Button button_1 (.out(reset));
  assign bit_extender_1_out = {{8{1'b0}}, subaddr};  // Bit_Extender bit_extender_1
  assign bit_extender_2_out = {{7{1'b0}}, mainaddr};  // Bit_Extender bit_extender_2
  Pull_Resistor pull_resistor_1 (.node(pull_resistor_1_node));
  buf buffer_1 (pull_resistor_1_node, stop);
  Clock clock_1 (.out(clock_1_out));
  or or_1 (or_1_out, reset, res);
  Counter #(.max('h7f), .width(7)) counter_1 (
    .clr(or_1_out), .clk(clk), .Q(subaddr));  // open: load, up, count, D, carry
  Multiplier #(.width(15)) multiplier_1 (
    .a(15'h65), .b(bit_extender_2_out), .out(multiplier_1_out));  // open: cin, cout
  Button step (.out(step_out));
  and and_1 (and_1_out, ~pull_resistor_1_node, ~man_step, clock_1_out);  // AND_Gate
  Comparator #(.mode("unsigned")) comparator_1 (.a(8'ha), .b(ram_out), .eq(res));  // open: gt, lt
  Adder #(.width(15)) adder_1 (.a(bit_extender_1_out), .b(multiplier_1_out), .out(adder_1_out));  // open: cin, cout
  or or_2 (clk, step_out, and_1_out);
  Comparator #(.mode("unsigned"), .width(7)) comparator_2 (
    .a(r1), .b(subaddr), .gt(comparator_2_gt), .eq(comparator_2_eq), .lt(comparator_2_lt));
  RAM #(.addrWidth(15), .asyncread("true"), .\type ("nonvolatile")) ram_1 (
    .addr(adder_1_out), .we(and_4_out), .clk(clk), .din({8{1'b0}}), .dout(ram_out));  // open: oe
  and and_2 (and_2_out, comparator_5_eq, or_3_out, comparator_8_lt);
  or or_3 (or_3_out, comparator_2_gt, comparator_2_eq);
  Comparator #(.mode("unsigned")) comparator_3 (.a(mainaddr), .b(8'hc8), .eq(stop));  // open: gt, lt
  and and_3 (and_3_out, comparator_5_eq, comparator_2_lt, comparator_6_lt);
  Comparator #(.mode("unsigned"), .width(7)) comparator_4 (.a({7{1'b0}}), .b(subaddr));  // open: gt, eq, lt
  Comparator #(.mode("unsigned"), .width(2)) comparator_5 (
    .a(counter_2_q), .b(2'b10), .gt(comparator_5_gt), .eq(comparator_5_eq));  // open: lt
  Counter #(.max('h3), .width(2)) counter_2 (
    .Q(counter_2_q), .clk(or_1_out), .clr(reset));  // open: load, D, count, carry, up
  or or_4 (or_4_out, comparator_5_gt, reset);
  and and_4 (and_4_out, comparator_7_eq, comparator_9_eq);
  Counter #(.max('hc8)) counter_3 (
    .clr(reset), .clk(comparator_5_gt), .Q(mainaddr));  // open: load, up, count, D, carry
  Register register_1 (.D(ram_out), .en(and_2_out), .clk(clk), .Q(d3), .clr(or_4_out));
  Register register_2 (.D(ram_out), .en(and_3_out), .clk(clk), .Q(d2), .clr(or_4_out));
  Register register_3 (.D(ram_out), .en(comparator_7_lt), .clk(clk), .Q(d1), .clr(or_4_out));
  Comparator #(.mode("unsigned")) comparator_6 (.a(d2), .b(ram_out), .lt(comparator_6_lt));  // open: gt, eq
  Comparator #(.mode("unsigned")) comparator_7 (
    .a(d1), .b(ram_out), .eq(comparator_7_eq), .lt(comparator_7_lt));  // open: gt
  Comparator #(.mode("unsigned")) comparator_8 (.a(d3), .b(ram_out), .lt(comparator_8_lt));  // open: gt, eq
  Register #(.width(7)) register_4 (.D(subaddr), .en(comparator_7_lt), .clk(clk), .Q(r1), .clr(or_4_out));
  Register #(.width(7)) register_5 (.D(subaddr), .en(and_2_out), .clk(clk), .Q(r3), .clr(or_4_out));
  Register #(.width(7)) register_6 (.D(subaddr), .en(and_3_out), .clk(clk), .Q(r2), .clr(or_4_out));
  Comparator #(.width(7)) comparator_9 (.a(r1), .b(subaddr), .eq(comparator_9_eq));  // open: gt, lt
  Subtractor subtractor_1 (.a(d2), .b(8'h30), .out(subtractor_1_out));  // open: bin, bout
  Subtractor subtractor_2 (.a(d3), .b(8'h30), .out(subtractor_2_out));  // open: bin, bout
  Comparator #(.mode("unsigned"), .width(7)) comparator_10 (
    .a(r1), .b(r2), .gt(comparator_10_gt), .lt(comparator_10_lt));  // open: eq
  Comparator #(.mode("unsigned"), .width(7)) comparator_11 (
    .a(r1), .b(r3), .gt(comparator_11_gt), .lt(comparator_11_lt));  // open: eq
  Multiplexer #(.width(8)) multiplexer_1 (
    .in0(subtractor_1_out), .in1(subtractor_3_out), .out(multiplexer_1_out), .sel(comparator_10_lt));
  Multiplexer #(.width(8)) multiplexer_2 (
    .in0(subtractor_1_out), .in1(subtractor_3_out), .out(multiplexer_2_out), .sel(comparator_10_gt));
  Subtractor subtractor_3 (.a(d1), .b(8'h30), .out(subtractor_3_out));  // open: bin, bout
  Multiplexer #(.width(8)) multiplexer_3 (
    .in0(subtractor_2_out), .in1(subtractor_4_out), .out(multiplexer_3_out), .sel(comparator_11_lt));
  Multiplexer #(.width(8)) multiplexer_4 (
    .in0(subtractor_2_out), .in1(subtractor_4_out), .out(multiplexer_4_out), .sel(comparator_11_gt));
  Subtractor subtractor_4 (.a(d1), .b(8'h30), .out(subtractor_4_out));  // open: bin, bout
  Multiplier multiplier_2 (.a(multiplexer_1_out), .b(8'ha), .out(multiplier_2_out));  // open: cin, cout
  Multiplier multiplier_3 (.a(multiplexer_3_out), .b(8'ha), .out(multiplier_3_out));  // open: cin, cout
  Adder adder_2 (.a(multiplier_2_out), .b(multiplexer_2_out), .out(out_3));  // open: cin, cout
  Adder adder_3 (.a(multiplier_3_out), .b(multiplexer_4_out), .out(out_2));  // open: cin, cout
  Comparator #(.mode("unsigned")) comparator_12 (
    .a(out_2), .b(out_3), .eq(comparator_12_eq), .lt(comparator_12_lt));  // open: gt
  assign bit_extender_3_out = {{8{1'b0}}, multiplexer_5_out};  // Bit_Extender bit_extender_3
  or or_5 (or_5_out, comparator_12_eq, comparator_12_lt);
  Adder #(.width(16)) adder_4 (.a(bit_extender_3_out), .b(register_7_q), .out(out_4));  // open: cin, cout
  Register #(.width(16)) register_7 (.D(out_4), .en(1'b1), .clk(comparator_5_gt), .Q(register_7_q), .clr(reset));
  Multiplexer #(.width(8)) multiplexer_5 (.in0(out_2), .in1(out_3), .out(multiplexer_5_out), .sel(or_5_out));
endmodule
